// Logisim project PC.circ as structural Verilog: 6 circuits, main circuit main
module main (
  output [15:0] out_1,
  output [15:0] out_2
);

  wire button_1_out, clock_1_out, processor_1_mem_r_w;
  wire [15:0] memory_1_data_out;

  Clock clock_1 (.out(clock_1_out));
  Button button_1 (.out(button_1_out));
  Processor processor_1 (
    .Clock(clock_1_out), .Reset(button_1_out), .Address(out_1), .Data_Out(out_2),
    .Data_In(memory_1_data_out), .Mem_R_W(processor_1_mem_r_w));
  Memory memory_1 (
    .Address(out_1), .CLOCK(clock_1_out), .E(1'b1), .R_W(processor_1_mem_r_w), .Data_In(out_2),
    .Data_Out(memory_1_data_out));  // open: in_1
endmodule

module Processor (
  input  Clock,
  input  Reset,
  input  [15:0] Data_In,
  output [15:0] Address,
  output Mem_R_W,
  output [15:0] Data_Out
);

  wire D1, D2, DATA, EW, IP, MUX_A, MUX_Address, MUX_OP, not_1_out, OP_r1, OP_r2;
  wire [1:0] MUX_B, MUX_DW;
  wire [3:0] control_unit_1_p16, undriven;
  wire [15:0] A_IP, alu_1_flags, alu_1_out_6, ALU_OUT, controlled_buffer_1_out, Data_Out_t,
       multiplexer_1_out, multiplexer_2_out, multiplexer_3_out, multiplexer_4_out, OP_1, OP_2, register_3_q,
       register_4_a, register_4_b, register_5_q;

  assign controlled_buffer_1_out = Mem_R_W ? Data_In : 16'bz;  // Controlled_Buffer controlled_buffer_1
  not not_1 (not_1_out, Mem_R_W);
  assign Data_Out = not_1_out ? Data_Out_t : 16'bz;  // Controlled_Buffer controlled_buffer_2
  Register_part #(.width(16)) register_1 (.D(controlled_buffer_1_out), .en(OP_r1), .Q(OP_1), .clk(Clock), .clr(Reset));
  Register_part #(.width(16)) register_2 (.D(controlled_buffer_1_out), .en(OP_r2), .Q(OP_2), .clk(Clock), .clr(Reset));
  Register_part #(.width(16)) register_3 (
    .D(controlled_buffer_1_out), .en(DATA), .Q(register_3_q), .clk(Clock), .clr(Reset));
  // Control_Unit control_unit_1: pin names not known; wires that end beside it: OP_1, OP_2, IP, OP_r1, OP_r2, DATA, EW, D1, D2, MUX_DW, MUX_A, MUX_B, MUX_OP, MUX_Address, Mem_R_W, control_unit_1_p16
  Multiplexer #(.select(2), .width(16)) multiplexer_1 (
    .in1(ALU_OUT), .in2(register_3_q), .out(multiplexer_1_out), .sel(MUX_DW), .en(1'b1));  // open: in0, in3
  Register register_4 (
    .A1(OP_1[7:4]), .in_4(EW), .A3(OP_1[15:12]), .DW(multiplexer_1_out), .A2(OP_1[11:8]), .A(register_4_a),
    .B(register_4_b), .in_1(Clock), .in_2(Reset));
  Register_part #(.width(16)) register_5 (.D(register_4_a), .en(D1), .Q(register_5_q), .clk(Clock), .clr(Reset));
  Register_part #(.width(16)) register_6 (.D(register_4_b), .en(D2), .Q(Data_Out_t), .clk(Clock), .clr(Reset));
  Multiplexer #(.width(16)) multiplexer_2 (
    .in0(A_IP), .in1(register_5_q), .out(multiplexer_2_out), .sel(MUX_A), .en(1'b1));
  Multiplexer #(.select(2), .width(16)) multiplexer_3 (
    .in0(16'h1), .in1(Data_Out_t), .out(multiplexer_3_out), .sel(MUX_B), .en(1'b1));  // open: in2, in3
  ALU alu_1 (
    .A(multiplexer_2_out), .B(multiplexer_3_out), .ALU_OP(control_unit_1_p16), .in_5(undriven),
    .out_6(alu_1_out_6), .FLAGS(alu_1_flags), .Ci(1'b0));
  Multiplexer #(.width(16)) multiplexer_4 (
    .in0(alu_1_out_6), .in1(ALU_OUT), .out(multiplexer_4_out), .sel(MUX_OP), .en(1'b1));
  Register_part #(.width(16)) register_7 (.D(alu_1_out_6), .Q(ALU_OUT));  // open: en, clk, clr
  Register_part #(.width(16)) register_8 (.D(multiplexer_4_out), .en(IP), .Q(A_IP), .clk(Clock), .clr(Reset));
  Multiplexer #(.width(16)) multiplexer_5 (.in0(A_IP), .in1(ALU_OUT), .out(Address), .sel(MUX_Address), .en(1'b1));

  // Other names for the same wires on the sheet: CLK = Clock; Res = Reset
endmodule

module Memory (
  input  [15:0] in_1,
  input  [15:0] Address,
  input  CLOCK,
  input  E,
  input  R_W,
  input  [15:0] Data_In,
  output [15:0] Data_Out
);

  wire not_1_out;
  wire [3:0] multiplexer_1_out_2;
  wire [15:0] multiplexer_1_out, ram_2_data;

  RAM #(.addrWidth(16)) ram_1 (
    .addr({in_1[15:1], 1'b0}), .data(ram_2_data[7:0]), .sel(E), .clk(CLOCK), .ld(R_W), .clr(1'b0));
  RAM #(.addrWidth(16)) ram_2 (
    .addr({1'b0, in_1[15:1]}), .data(ram_2_data[15:8]), .sel(E), .clk(CLOCK), .ld(R_W), .clr(1'b0));
  Hex_Digit_Display hex_digit_display_1 (.value(multiplexer_1_out_2));  // open: dp
  Hex_Digit_Display hex_digit_display_2 (.value(multiplexer_1_out[3:0]));  // open: dp
  Multiplexer #(.width(16)) multiplexer_1 (
    .in0(ram_2_data), .in1({ram_2_data[7:0], ram_2_data[15:8]}),
    .out({multiplexer_1_out[15:8], multiplexer_1_out_2, multiplexer_1_out[3:0]}), .sel(in_1[0]), .en(1'b1));
  Hex_Digit_Display hex_digit_display_3 (.value(multiplexer_1_out[11:8]));  // open: dp
  Hex_Digit_Display hex_digit_display_4 (.value(multiplexer_1_out[15:12]));  // open: dp
  not not_1 (not_1_out, R_W);
  assign {multiplexer_1_out[15:8], multiplexer_1_out_2, multiplexer_1_out[3:0]} = not_1_out ? Data_In : 16'bz;  // Controlled_Buffer controlled_buffer_1
  assign Data_Out = R_W ? {multiplexer_1_out[15:8], multiplexer_1_out_2, multiplexer_1_out[3:0]} : 16'bz;  // Controlled_Buffer controlled_buffer_2
endmodule

module Register (
  input  in_1,
  input  in_2,
  input  [3:0] A1,
  input  in_4,
  input  [3:0] A3,
  input  [15:0] DW,
  input  [3:0] A2,
  output [15:0] A,
  output [15:0] B
);

  wire decoder_2_out0, decoder_2_out1, decoder_2_out2, decoder_2_out3, decoder_2_out4, decoder_2_out5,
       decoder_2_out6, decoder_2_out7, decoder_2_out8, decoder_2_out9, decoder_2_out10, decoder_2_out11,
       decoder_2_out12, decoder_2_out13, decoder_2_out14, decoder_2_out15, decoder_3_out0, decoder_3_out1,
       decoder_3_out2, decoder_3_out3, decoder_3_out4, decoder_3_out5, decoder_3_out6, decoder_3_out7,
       decoder_3_out8, decoder_3_out9, decoder_3_out10, decoder_3_out11, decoder_3_out12, decoder_3_out13,
       decoder_3_out14, decoder_3_out15, pull_resistor_1_node, pull_resistor_2_node, pull_resistor_3_node,
       pull_resistor_4_node, pull_resistor_5_node, pull_resistor_6_node, pull_resistor_7_node,
       pull_resistor_8_node, pull_resistor_9_node, pull_resistor_10_node, pull_resistor_11_node,
       pull_resistor_12_node, pull_resistor_13_node, pull_resistor_14_node, pull_resistor_15_node,
       pull_resistor_16_node;
  wire [15:0] register_1_q, register_2_q, register_3_q, register_4_q, register_5_q, register_6_q,
       register_7_q, register_8_q, register_9_q, register_10_q, register_11_q, register_12_q, register_13_q,
       register_14_q, register_15_q, register_16_q;

  Pull_Resistor pull_resistor_1 (.node(pull_resistor_1_node));
  Pull_Resistor pull_resistor_2 (.node(pull_resistor_2_node));
  Pull_Resistor pull_resistor_3 (.node(pull_resistor_3_node));
  Pull_Resistor pull_resistor_4 (.node(pull_resistor_4_node));
  Pull_Resistor pull_resistor_5 (.node(pull_resistor_5_node));
  Pull_Resistor pull_resistor_6 (.node(pull_resistor_6_node));
  Pull_Resistor pull_resistor_7 (.node(pull_resistor_7_node));
  Pull_Resistor pull_resistor_8 (.node(pull_resistor_8_node));
  Pull_Resistor pull_resistor_9 (.node(pull_resistor_9_node));
  Pull_Resistor pull_resistor_10 (.node(pull_resistor_10_node));
  Pull_Resistor pull_resistor_11 (.node(pull_resistor_11_node));
  Pull_Resistor pull_resistor_12 (.node(pull_resistor_12_node));
  Pull_Resistor pull_resistor_13 (.node(pull_resistor_13_node));
  Pull_Resistor pull_resistor_14 (.node(pull_resistor_14_node));
  Pull_Resistor pull_resistor_15 (.node(pull_resistor_15_node));
  Pull_Resistor pull_resistor_16 (.node(pull_resistor_16_node));
  Decoder #(.select(4)) decoder_1 (
    .out0(pull_resistor_1_node), .out1(pull_resistor_2_node), .out2(pull_resistor_3_node),
    .out3(pull_resistor_4_node), .out4(pull_resistor_5_node), .out5(pull_resistor_6_node),
    .out6(pull_resistor_7_node), .out7(pull_resistor_8_node), .out8(pull_resistor_9_node),
    .out9(pull_resistor_10_node), .out10(pull_resistor_11_node), .out11(pull_resistor_12_node),
    .out12(pull_resistor_13_node), .out13(pull_resistor_14_node), .out14(pull_resistor_15_node),
    .out15(pull_resistor_16_node), .sel(A3), .en(in_4));
  Decoder #(.select(4)) decoder_2 (
    .out0(decoder_2_out0), .out1(decoder_2_out1), .out2(decoder_2_out2), .out3(decoder_2_out3),
    .out4(decoder_2_out4), .out5(decoder_2_out5), .out6(decoder_2_out6), .out7(decoder_2_out7),
    .out8(decoder_2_out8), .out9(decoder_2_out9), .out10(decoder_2_out10), .out11(decoder_2_out11),
    .out12(decoder_2_out12), .out13(decoder_2_out13), .out14(decoder_2_out14), .out15(decoder_2_out15),
    .sel(A2), .en(1'b1));
  Decoder #(.select(4)) decoder_3 (
    .out0(decoder_3_out0), .out1(decoder_3_out1), .out2(decoder_3_out2), .out3(decoder_3_out3),
    .out4(decoder_3_out4), .out5(decoder_3_out5), .out6(decoder_3_out6), .out7(decoder_3_out7),
    .out8(decoder_3_out8), .out9(decoder_3_out9), .out10(decoder_3_out10), .out11(decoder_3_out11),
    .out12(decoder_3_out12), .out13(decoder_3_out13), .out14(decoder_3_out14), .out15(decoder_3_out15),
    .sel(A1), .en(1'b1));
  Register_part #(.width(16)) register_1 (.D(DW), .en(pull_resistor_1_node), .Q(register_1_q), .clk(in_1), .clr(in_2));
  Register_part #(.width(16)) register_2 (.D(DW), .en(pull_resistor_2_node), .Q(register_2_q), .clk(in_1), .clr(in_2));
  Register_part #(.width(16)) register_3 (.D(DW), .en(pull_resistor_3_node), .Q(register_3_q), .clk(in_1), .clr(in_2));
  Register_part #(.width(16)) register_4 (.D(DW), .en(pull_resistor_4_node), .Q(register_4_q), .clk(in_1), .clr(in_2));
  Register_part #(.width(16)) register_5 (.D(DW), .en(pull_resistor_5_node), .Q(register_5_q), .clk(in_1), .clr(in_2));
  Register_part #(.width(16)) register_6 (.D(DW), .en(pull_resistor_6_node), .Q(register_6_q), .clk(in_1), .clr(in_2));
  Register_part #(.width(16)) register_7 (.D(DW), .en(pull_resistor_7_node), .Q(register_7_q), .clk(in_1), .clr(in_2));
  Register_part #(.width(16)) register_8 (.D(DW), .en(pull_resistor_8_node), .Q(register_8_q), .clk(in_1), .clr(in_2));
  Register_part #(.width(16)) register_9 (.D(DW), .en(pull_resistor_9_node), .Q(register_9_q), .clk(in_1), .clr(in_2));
  Register_part #(.width(16)) register_10 (
    .D(DW), .en(pull_resistor_10_node), .Q(register_10_q), .clk(in_1), .clr(in_2));
  Register_part #(.width(16)) register_11 (
    .D(DW), .en(pull_resistor_11_node), .Q(register_11_q), .clk(in_1), .clr(in_2));
  Register_part #(.width(16)) register_12 (
    .D(DW), .en(pull_resistor_12_node), .Q(register_12_q), .clk(in_1), .clr(in_2));
  Register_part #(.width(16)) register_13 (
    .D(DW), .en(pull_resistor_13_node), .Q(register_13_q), .clk(in_1), .clr(in_2));
  Register_part #(.width(16)) register_14 (
    .D(DW), .en(pull_resistor_14_node), .Q(register_14_q), .clk(in_1), .clr(in_2));
  Register_part #(.width(16)) register_15 (
    .D(DW), .en(pull_resistor_15_node), .Q(register_15_q), .clk(in_1), .clr(in_2));
  Register_part #(.width(16)) register_16 (
    .D(DW), .en(pull_resistor_16_node), .Q(register_16_q), .clk(in_1), .clr(in_2));
  assign A = decoder_3_out0 ? register_1_q : 16'bz;  // Controlled_Buffer controlled_buffer_1
  assign B = decoder_2_out0 ? register_1_q : 16'bz;  // Controlled_Buffer controlled_buffer_2
  assign A = decoder_3_out1 ? register_2_q : 16'bz;  // Controlled_Buffer controlled_buffer_3
  assign B = decoder_2_out1 ? register_2_q : 16'bz;  // Controlled_Buffer controlled_buffer_4
  assign A = decoder_3_out2 ? register_3_q : 16'bz;  // Controlled_Buffer controlled_buffer_5
  assign B = decoder_2_out2 ? register_3_q : 16'bz;  // Controlled_Buffer controlled_buffer_6
  assign A = decoder_3_out3 ? register_4_q : 16'bz;  // Controlled_Buffer controlled_buffer_7
  assign B = decoder_2_out3 ? register_4_q : 16'bz;  // Controlled_Buffer controlled_buffer_8
  assign A = decoder_3_out4 ? register_5_q : 16'bz;  // Controlled_Buffer controlled_buffer_9
  assign B = decoder_2_out4 ? register_5_q : 16'bz;  // Controlled_Buffer controlled_buffer_10
  assign A = decoder_3_out5 ? register_6_q : 16'bz;  // Controlled_Buffer controlled_buffer_11
  assign B = decoder_2_out5 ? register_6_q : 16'bz;  // Controlled_Buffer controlled_buffer_12
  assign A = decoder_3_out6 ? register_7_q : 16'bz;  // Controlled_Buffer controlled_buffer_13
  assign B = decoder_2_out6 ? register_7_q : 16'bz;  // Controlled_Buffer controlled_buffer_14
  assign A = decoder_3_out7 ? register_8_q : 16'bz;  // Controlled_Buffer controlled_buffer_15
  assign B = decoder_2_out7 ? register_8_q : 16'bz;  // Controlled_Buffer controlled_buffer_16
  assign A = decoder_3_out8 ? register_9_q : 16'bz;  // Controlled_Buffer controlled_buffer_17
  assign B = decoder_2_out8 ? register_9_q : 16'bz;  // Controlled_Buffer controlled_buffer_18
  assign A = decoder_3_out9 ? register_10_q : 16'bz;  // Controlled_Buffer controlled_buffer_19
  assign B = decoder_2_out9 ? register_10_q : 16'bz;  // Controlled_Buffer controlled_buffer_20
  assign A = decoder_3_out10 ? register_11_q : 16'bz;  // Controlled_Buffer controlled_buffer_21
  assign B = decoder_2_out10 ? register_11_q : 16'bz;  // Controlled_Buffer controlled_buffer_22
  assign A = decoder_3_out11 ? register_12_q : 16'bz;  // Controlled_Buffer controlled_buffer_23
  assign B = decoder_2_out11 ? register_12_q : 16'bz;  // Controlled_Buffer controlled_buffer_24
  assign A = decoder_3_out12 ? register_13_q : 16'bz;  // Controlled_Buffer controlled_buffer_25
  assign B = decoder_2_out12 ? register_13_q : 16'bz;  // Controlled_Buffer controlled_buffer_26
  assign A = decoder_3_out13 ? register_14_q : 16'bz;  // Controlled_Buffer controlled_buffer_27
  assign B = decoder_2_out13 ? register_14_q : 16'bz;  // Controlled_Buffer controlled_buffer_28
  assign A = decoder_3_out14 ? register_15_q : 16'bz;  // Controlled_Buffer controlled_buffer_29
  assign B = decoder_2_out14 ? register_15_q : 16'bz;  // Controlled_Buffer controlled_buffer_30
  assign A = decoder_3_out15 ? register_16_q : 16'bz;  // Controlled_Buffer controlled_buffer_31
  assign B = decoder_2_out15 ? register_16_q : 16'bz;  // Controlled_Buffer controlled_buffer_32
endmodule

module ALU (
  input  Ci,
  input  [15:0] A,
  input  [15:0] B,
  input  [3:0] ALU_OP,
  input  [3:0] in_5,
  output [15:0] out_6,
  output [15:0] FLAGS
);

  wire adder_1_cout, and_1_out, and_3_out, and_4_out, not_2_out, not_3_out, not_4_out, or_1_out, xor_1_out;
  wire [15:0] adder_1_out, and_2_out, multiplexer_1_out, not_1_out, or_2_out, shifter_1_out, shifter_2_out,
       shifter_3_out, xor_3_out;

  or or_1 (or_1_out, Ci, ALU_OP[2]);
  and and_1 (and_1_out, or_1_out, ALU_OP[0]);
  assign not_1_out = ~B;  // NOT_Gate not_1, 16 bits wide
  xor xor_1 (xor_1_out, and_1_out, ALU_OP[1]);
  Multiplexer #(.width(16)) multiplexer_1 (
    .in0(B), .in1(not_1_out), .out(multiplexer_1_out), .sel(ALU_OP[1]), .en(1'b1));
  Adder #(.width(16)) adder_1 (.a(A), .b(multiplexer_1_out), .out(adder_1_out), .cin(xor_1_out), .cout(adder_1_cout));
  xor xor_2 (FLAGS[1], adder_1_cout, ALU_OP[1]);
  assign and_2_out = A & multiplexer_1_out;  // AND_Gate and_2, 16 bits wide
  assign or_2_out = A | multiplexer_1_out;  // OR_Gate or_2, 16 bits wide
  assign xor_3_out = A ^ multiplexer_1_out;  // XOR_Gate xor_3, 16 bits wide
  Shifter #(.width(16), .shift("lr")) shifter_1 (.in(A), .\dist (in_5), .out(shifter_1_out));
  Shifter #(.width(16)) shifter_2 (.in(A), .\dist (in_5), .out(shifter_2_out));
  Shifter #(.width(16), .shift("ar")) shifter_3 (.in(A), .\dist (in_5), .out(shifter_3_out));
  not not_2 (not_2_out, FLAGS[2]);
  not not_3 (not_3_out, B[15]);
  not not_4 (not_4_out, A[15]);
  and and_3 (and_3_out, not_3_out, A[15], not_2_out);
  and and_4 (and_4_out, B[15], not_4_out, FLAGS[2]);
  or or_3 (FLAGS[3], and_4_out, and_3_out);
  Multiplexer #(.select(4), .width(16)) multiplexer_2 (
    .in0(adder_1_out), .in1(adder_1_out), .in2(adder_1_out), .in3(adder_1_out), .in4(and_2_out),
    .in5(or_2_out), .in6(xor_3_out), .in7(adder_1_out), .in8(shifter_1_out), .in9(shifter_2_out),
    .in10(shifter_3_out), .out({FLAGS[2], out_6[14:0]}), .sel(ALU_OP), .en(1'b1));  // open: in11, in12, in13, in14, in15
  Comparator #(.width(16)) comparator_1 (.a({FLAGS[2], out_6[14:0]}), .b({16{1'b0}}), .eq(FLAGS[0]));  // open: gt, lt

  assign FLAGS[15:4] = {12{1'b0}};
  assign out_6[15] = FLAGS[2];
endmodule

module Control_Unit (
  input  [15:0] OP_1,
  input  [15:0] OP_2,
  output IP,
  output OP_r1,
  output OP_r2,
  output DATA,
  output EW,
  output D1,
  output D2,
  output [1:0] MUX_DW,
  output MUX_A,
  output [1:0] MUX_B,
  output MUX_OP,
  output MUX_Address,
  output Mem_R_W,
  output [3:0] ALU_OP
);

  wire decoder_1_out0, decoder_1_out1;
  wire [4:0] register_1_q, undriven;

  Register_part #(.width(5)) register_1 (.D(undriven), .Q(register_1_q));  // open: en, clk, clr
  Decoder #(.select(5)) decoder_1 (
    .out0(decoder_1_out0), .out1(decoder_1_out1), .sel(register_1_q), .en(1'b1));  // open: out2, out3, out4, out5, out6, out7, out8, out9, out10, out11, out12, out13, out14, out15, out16, out17, out18, out19, out20, out21, out22, out23, out24, out25, out26, out27, out28, out29, out30, out31
  buf or_1 (OP_r1, decoder_1_out0);  // OR_Gate
  or or_2 (IP, decoder_1_out0, decoder_1_out1);
  buf or_3 (OP_r2, decoder_1_out1);  // OR_Gate
  buf or_4 (MUX_B[1], 1'b0);  // OR_Gate
  buf or_5 (MUX_B[0], 1'b0);  // OR_Gate
  or or_6 (Mem_R_W, decoder_1_out0, decoder_1_out1);

  assign ALU_OP = 4'b0000;
  assign D1 = 1'b0;
  assign D2 = 1'b0;
  assign DATA = 1'b0;
  assign EW = 1'b0;
  assign MUX_A = 1'b0;
  assign MUX_Address = 1'b0;
  assign MUX_DW = 2'b00;
  assign MUX_OP = 1'b0;
endmodule
